// Logisim project incrementer.circ as structural Verilog: 4 circuits, main circuit main
module main (
  input  A10,
  input  A9,
  input  A8,
  input  A7,
  input  A6,
  input  A5,
  input  A4,
  input  A3,
  input  A2,
  input  A1,
  input  A0,
  output X10,
  output X9,
  output X8,
  output X7,
  output X6,
  output X5,
  output X4,
  output X3,
  output X2,
  output X1,
  output X0
);

  wire [10:0] clsh1_1_y, clsh1_2_y, clsh1_3_y, clsh1_4_y, clsh1_5_y, clsh1_6_y, clsh1_7_y, clsh1_8_y,
       clsh1_9_y, clsh1_10_y;

  CLSH1 clsh1_1 (.X({A10, A9, A8, A7, A6, A5, A4, A3, A2, A1, A0}), .Y(clsh1_1_y));
  CLSH1 clsh1_2 (.X(clsh1_1_y), .Y(clsh1_2_y));
  CLSH1 clsh1_3 (.X(clsh1_2_y), .Y(clsh1_3_y));
  CLSH1 clsh1_4 (.X(clsh1_3_y), .Y(clsh1_4_y));
  CLSH1 clsh1_5 (.X(clsh1_4_y), .Y(clsh1_5_y));
  CLSH1 clsh1_6 (.X(clsh1_5_y), .Y(clsh1_6_y));
  CLSH1 clsh1_7 (.X(clsh1_6_y), .Y(clsh1_7_y));
  CLSH1 clsh1_8 (.X(clsh1_7_y), .Y(clsh1_8_y));
  CLSH1 clsh1_9 (.X(clsh1_8_y), .Y(clsh1_9_y));
  CLSH1 clsh1_10 (.X(clsh1_9_y), .Y(clsh1_10_y));
  CLSH1 clsh1_11 (.X(clsh1_10_y), .Y({X10, X9, X8, X7, X6, X5, X4, X3, X2, X1, X0}));

  // Notes on the sheet:
  //   Do not introduce any other input or output pins in the main circuit.
  //   INPUT SECTION: Do not change anything here!
  //   You may only change the values of the inputs for testing using the hand tool.
  //   The output of the splitter (11 bits wide) should be the input to your logic.
  //   To your logic
  //   From your logic
  //   OUTPUT SECTION: Do not change anything here!
  //   Do not introduce any other input or output pins in the main circuit.
  //   The input to the splitter (11 bits wide) should come from the output of your logic.
endmodule

module LSH1 (
  input  [10:0] in_1,
  output [10:0] out_2
);


  assign out_2 = {in_1[9:0], 1'b0};
endmodule

module Mux11 (
  input  [10:0] A,
  input  S,
  input  [10:0] B,
  output [10:0] Output
);

  wire [10:0] and_1_out, and_2_out;
  wire [10:10] not_1_out;

  not not_1 (not_1_out[10], S);
  assign and_1_out = A & {11{not_1_out[10]}};  // AND_Gate and_1, 11 bits wide
  assign and_2_out = {11{S}} & B;  // AND_Gate and_2, 11 bits wide
  assign Output = and_1_out | and_2_out;  // OR_Gate or_1, 11 bits wide
endmodule

module CLSH1 (
  input  [10:0] X,
  output [10:0] Y
);

  wire [10:0] lsh1_1_out_2;

  LSH1 lsh1_1 (.in_1(X), .out_2(lsh1_1_out_2));
  Mux11 mux11_1 (.A(lsh1_1_out_2), .S(X[10]), .B(X), .Output(Y));
endmodule
