// Logisim project H2.circ as structural Verilog: 2 circuits, main circuit P2
module P2 (
  input  S1,
  input  S0,
  input  In,
  output S1n,
  output S0n,
  output Out
);

  wire A_2_out, A_out, B_2_out, B_out, C_out, D_2_out, D_out;

  and A (A_out, ~S0, ~S1, ~In);  // AND_Gate
  and B (B_out, S0, ~S1, ~In);  // AND_Gate
  and C (C_out, ~S0, S1, ~In);  // AND_Gate
  and D (D_out, S0, S1, ~In);  // AND_Gate
  and A_2 (A_2_out, ~S0, ~S1, In);  // AND_Gate
  and B_2 (B_2_out, S0, ~S1, In);  // AND_Gate
  and D_2 (D_2_out, S0, S1, In);
  or u_S1 (S1n, A_out, C_out, D_out);
  or u_S0 (S0n, C_out, B_2_out, A_2_out);
  or u_Out (Out, C_out, A_2_out, D_2_out, D_out, B_out);

  // Notes on the sheet:
  //   PROBLEM 2: IMPLEMENTING A STATE TABLE
  //   INPUT SECTION: Do not change anything here!
  //   You may only change the values of the inputs for testing using the hand tool.
  //   Do not introduce any other input or output pins in the circuit.
  //   To your logic
  //   OUTPUT SECTION: Do not change anything here!
  //   Do not introduce any other input or output pins in the circuit.
  //   From your logic
endmodule

module P3 (
  input  In,
  output Out,
  output s2,
  output s1,
  output s0
);

  wire _0_out, _1_out, _2_out, A_out, B_out, C_out, clock_1_out, D_2_out, D_out, E_2_out, E_out, F_2_out,
       F_out, G_out, or_1_out, or_2_out;

  and A (A_out, ~In, ~s2, ~s1, ~s0);  // AND_Gate
  and B (B_out, ~In, s2, ~s1, ~s0);  // AND_Gate
  and C (C_out, ~In, ~s2, s1, ~s0);  // AND_Gate
  and D (D_out, ~In, ~s2, ~s1, s0);  // AND_Gate
  and E (E_out, ~In, s2, ~s1, s0);  // AND_Gate
  and F (F_out, ~In, ~s2, s1, s0);  // AND_Gate
  and G (G_out, ~In, s2, s1, ~s0);  // AND_Gate
  and D_2 (D_2_out, In, ~s2, ~s1, s0);  // AND_Gate
  and E_2 (E_2_out, In, s2, ~s1, s0);  // AND_Gate
  and F_2 (F_2_out, In, ~s2, s1, s0);  // AND_Gate
  or or_1 (or_1_out, G_out, A_out);
  or or_2 (or_2_out, D_out, E_out);
  Clock clock_1 (.out(clock_1_out));
  or _0 (_0_out, C_out, or_2_out, D_2_out, E_2_out);
  or _1 (_1_out, E_2_out, B_out, F_2_out);
  or _2 (_2_out, F_2_out, or_2_out, or_1_out, F_out);
  D_Flip_Flop u_S0 (.clk(clock_1_out), .D(_0_out), .Q(s0));  // open: Qn, preset, en, reset
  D_Flip_Flop u_S1 (.clk(clock_1_out), .D(_1_out), .Q(s1));  // open: Qn, preset, en, reset
  D_Flip_Flop u_S2 (.clk(clock_1_out), .D(_2_out), .Q(s2));  // open: Qn, preset, en, reset
  and and_1 (Out, s2, s1, ~s0);  // AND_Gate

  // Notes on the sheet:
  //   PROBLEM 3: IMPLEMENTING A STATE MACHINE
  //   INPUT SECTION: Do not change anything here!
  //   You may only change the values of the inputs for testing using the hand tool.
  //   Do not introduce any other input or output pins in the circuit.
  //   To your logic
  //   OUTPUT SECTION: Do not change anything here!
  //   Do not introduce any other input or output pins in the circuit.
  //   From your logic
endmodule
