// Logisim project hghj.circ as structural Verilog: 2 circuits, main circuit main
module main (
  input  a,
  input  b,
  input  c,
  output x
);

  wire and_1_out, and_2_out, not_1_out;

  not not_1 (not_1_out, b);
  and and_1 (and_1_out, b, a, c);
  and and_2 (and_2_out, c, a, not_1_out);
  or or_1 (x, and_1_out, and_2_out);
endmodule

module sd (
  input  a,
  input  b,
  output x,
  output y,
  output z,
  output u
);

  wire not_1_out, not_2_out, not_3_out, not_4_out;

  not not_1 (not_1_out, a);
  not not_2 (not_2_out, b);
  not not_3 (not_3_out, a);
  not not_4 (not_4_out, b);
  and and_1 (u, a, b);
  and and_2 (x, not_1_out, not_2_out);
  and and_3 (y, not_3_out, b);
  and and_4 (z, a, not_4_out);
endmodule
