// Logisim project two.circ as structural Verilog: 1 circuit, main circuit main
module main (
  input  C,
  input  C_2,
  input  A,
  input  in_4,
  input  in_5,
  output X,
  output out_7,
  output out_8
);

  wire and_1_out, and_2_out, and_3_out, and_4_out, and_5_out, and_7_out, not_1_out, not_2_out, not_3_out,
       not_4_out, not_5_out, not_6_out, not_7_out, not_8_out, not_9_out, not_10_out, not_11_out, undriven,
       undriven_2, undriven_3;

  and and_1 (and_1_out, undriven, undriven_2, undriven_3);
  not not_1 (not_1_out, undriven);
  and and_2 (and_2_out, not_1_out, undriven_2, undriven_3);
  and and_3 (and_3_out, not_2_out, not_3_out, undriven_3);
  not not_2 (not_2_out, undriven);
  not not_3 (not_3_out, undriven_2);
  not not_4 (not_4_out, undriven);
  and and_4 (and_4_out, not_4_out, undriven_2, not_5_out);
  not not_5 (not_5_out, undriven_3);
  and and_5 (and_5_out, undriven, not_6_out, not_7_out);
  not not_6 (not_6_out, undriven_2);
  not not_7 (not_7_out, undriven_3);
  and and_6 (out_7, not_8_out, not_9_out, not_10_out);
  not not_8 (not_8_out, undriven);
  not not_9 (not_9_out, undriven_2);
  not not_10 (not_10_out, undriven_3);
  not not_11 (not_11_out, in_5);
  and and_7 (and_7_out, in_4, not_11_out);
  buf or_1 (out_8, and_7_out);  // OR_Gate
  or or_2 (X, and_1_out, and_2_out, and_3_out, and_4_out, and_5_out);
endmodule
