// Logisim project R18.circ as structural Verilog: 3 circuits, main circuit E3_Main
module E3_Main (
  input  A7,
  input  A6,
  input  A5,
  input  A4,
  input  A3,
  input  A2,
  input  A1,
  input  A0,
  output X7,
  output X6,
  output X5,
  output X4,
  output X3,
  output X2,
  output X1,
  output X0
);

  wire e3_decrbit0_1_xout, e3_decronebit_1_xout, e3_decronebit_2_xout, e3_decronebit_3_xout,
       e3_decronebit_4_xout, e3_decronebit_5_xout, e3_decronebit_6_xout;

  E3_DecrBit0 e3_decrbit0_1 (.A(A0), .S(X0), .Xout(e3_decrbit0_1_xout));
  E3_DecrOneBit e3_decronebit_1 (.Xin(e3_decrbit0_1_xout), .A(A1), .S(X1), .Xout(e3_decronebit_1_xout));
  E3_DecrOneBit e3_decronebit_2 (.Xin(e3_decronebit_1_xout), .A(A2), .S(X2), .Xout(e3_decronebit_2_xout));
  E3_DecrOneBit e3_decronebit_3 (.Xin(e3_decronebit_2_xout), .A(A3), .S(X3), .Xout(e3_decronebit_3_xout));
  E3_DecrOneBit e3_decronebit_4 (.Xin(e3_decronebit_3_xout), .A(A4), .S(X4), .Xout(e3_decronebit_4_xout));
  E3_DecrOneBit e3_decronebit_5 (.Xin(e3_decronebit_4_xout), .A(A5), .S(X5), .Xout(e3_decronebit_5_xout));
  E3_DecrOneBit e3_decronebit_6 (.Xin(e3_decronebit_5_xout), .A(A6), .S(X6), .Xout(e3_decronebit_6_xout));
  E3_DecrOneBit e3_decronebit_7 (.Xin(e3_decronebit_6_xout), .A(A7), .S(X7));  // open: Xout

  // Notes on the sheet:
  //   EXERCISE 3: 8-BIT DECREMENTER (Main)
  //   INPUT SECTION: Do not change anything here!
  //   You may only change the values of the inputs for testing using the hand tool.
  //   Do not introduce any other input or output pins.
  //   To your logic
  //   OUTPUT SECTION: Do not change anything here!
  //   Do not introduce any other input or output pins.
  //   From your logic
endmodule

module E3_DecrOneBit (
  input  Xin,
  input  A,
  output S,
  output Xout
);

  wire and_1_out, not_1_out, not_2_out;

  not not_1 (not_1_out, Xin);
  not not_2 (not_2_out, A);
  and and_1 (and_1_out, not_1_out, A);
  and and_2 (Xout, Xin, not_2_out);
  or or_1 (S, and_1_out, Xout);

  // Notes on the sheet:
  //   EXERCISE 3: 8-BIT DECREMENTER (DecrOneBit)
  //   INPUT SECTION: Do not change anything here!
  //   You may only change the values of the inputs for testing using the hand tool.
  //   Do not introduce any other input or output pins.
  //   To your logic
  //   OUTPUT SECTION: Do not change anything here!
  //   Do not introduce any other input or output pins.
  //   From your logic
endmodule

module E3_DecrBit0 (
  input  A,
  output S,
  output Xout
);

  not not_1 (S, A);

  assign Xout = S;

  // Notes on the sheet:
  //   EXERCISE 3: 8-BIT DECREMENTER (DecrBit0)
  //   INPUT SECTION: Do not change anything here!
  //   You may only change the values of the inputs for testing using the hand tool.
  //   Do not introduce any other input or output pins.
  //   To your logic
  //   OUTPUT SECTION: Do not change anything here!
  //   Do not introduce any other input or output pins.
  //   From your logic
endmodule
